# Fritzing sketch raspif (saved by Fritzing 0.9.9b)
circuit board: 6.73681cm x 3.77968cm
breadboards: 3

parts:
  IC1 = ULN2803A [package=THT]
  U1 = 74LVC138AD [package=so016]
  LED1 = LED - 5mm [color="Red (633nm)" current=0.030 package="5 mm [THT]"]
  LED2 = LED - 5mm [color="Red (633nm)" current=0.030 package="5 mm [THT]"]
  LED3 = LED - 5mm [color="Red (633nm)" current=0.030 package="5 mm [THT]"]
  LED4 = LED - 5mm [color="Red (633nm)" current=0.030 package="5 mm [THT]"]
  LED5 = LED - 5mm [color="Red (633nm)" current=0.030 package="5 mm [THT]"]
  LED6 = LED - 5mm [color="Red (633nm)" current=0.030 package="5 mm [THT]"]
  LED7 = LED - 5mm [color="Red (633nm)" current=0.030 package="5 mm [THT]"]
  LED8 = LED - 5mm [color="Red (633nm)" current=0.030 package="5 mm [THT]"]
  R1 = Resistor [tolerance=±5% power=0.25 resistance=220 package=THT]

nets:
  N1: IC1.In_1, U1._Y0
  N2: IC1.In_2, U1._Y1
  N3: IC1.In_3, U1._Y2
  N4: IC1.In_4, U1._Y3
  N5: IC1.In_5, U1._Y4
  N6: IC1.In_6, U1._Y5
  N7: IC1.In_7, U1._Y6
  N8: IC1.In_8, U1._Y7
  GND: IC1.0V, U1.GND
  5V: IC1.COM_-_Common, U1.VCC, R1.Pin_1
  N9: IC1.Out_8, LED5.cathode
  N10: IC1.Out_7, LED8.cathode
  N11: IC1.Out_6, LED7.cathode
  N12: IC1.Out_5, LED6.cathode
  N13: IC1.Out_4, LED4.cathode
  N14: IC1.Out_3, LED3.cathode
  N15: IC1.Out_2, LED2.cathode
  N16: IC1.Out_1, LED1.cathode
  N17: LED1.anode, LED2.anode, LED3.anode, LED4.anode, LED5.anode, LED6.anode, LED7.anode, LED8.anode, R1.Pin_0
